// Logisim project projeto de circuito 2.circ as structural Verilog: 9 circuits, main circuit main
module main (
  input  Clock,
  input  SelecionaXouY,
  input  SelecionaAouB,
  input  in_4,
  input  in_5,
  input  in_6,
  input  in_7,
  input  in_8,
  input  in_9,
  input  in_10,
  input  in_11,
  input  in_12,
  input  in_13
);

  wire numerouser_1_out_7, numerouseroeste_1_out_7, Seletor_out_5, Seletor_out_7;
  wire [3:0] \Memoria4bits_saída , numerouser_1_out_6, numerouseroeste_1_out_6, Seletor_out_6, Seletor_out_8;
  wire [4:0] numerouser_1_s, numerouseroeste_1_s;

  LED led_1 (.in(numerouser_1_out_7));
  Hex_Digit_Display hex_digit_display_1 (.value(numerouser_1_out_6));  // open: dp
  NumeroUser numerouser_1 (
    .out_7(numerouser_1_out_7), .out_6(numerouser_1_out_6), .in_1(in_4), .in_2(in_5), .in_3(in_6),
    .in_4(in_7), .in_5(in_8), .S(numerouser_1_s));
  LED led_2 (.in(Seletor_out_5));
  Hex_Digit_Display hex_digit_display_2 (.value(\Memoria4bits_saída ));  // open: dp
  MemoriaNumeroUser Memoria4bits (.Entrada(Seletor_out_6), .Clock(Clock), .\Saída (\Memoria4bits_saída ));
  Hex_Digit_Display hex_digit_display_3 (.value(Seletor_out_8));  // open: dp
  LED led_3 (.in(Seletor_out_7));
  Seletor Seletor (
    .in_1(SelecionaXouY), .in_2(SelecionaAouB), .in_3(numerouser_1_s), .in_4(numerouseroeste_1_s),
    .out_6(Seletor_out_6), .out_8(Seletor_out_8), .out_5(Seletor_out_5), .out_7(Seletor_out_7));
  LED led_4 (.in(numerouseroeste_1_out_7));
  Hex_Digit_Display hex_digit_display_4 (.value(numerouseroeste_1_out_6));  // open: dp
  NumeroUserOeste numerouseroeste_1 (
    .S(numerouseroeste_1_s), .out_7(numerouseroeste_1_out_7), .out_6(numerouseroeste_1_out_6), .in_1(in_9),
    .in_2(in_10), .in_3(in_11), .in_4(in_12), .in_5(in_13));

  // Notes on the sheet:
  //   Jogador A
  //   X
  //   Y
  //   Jogador B
endmodule

module NumeroUser (
  input  in_1,
  input  in_2,
  input  in_3,
  input  in_4,
  input  in_5,
  output [3:0] out_6,
  output out_7,
  output [4:0] S
);


  assign out_6 = {in_2, in_3, in_4, in_5};
  assign out_7 = in_1;
  assign S = {in_1, in_2, in_3, in_4, in_5};
endmodule

// NumeroUser
module NumeroUserOeste (
  input  in_1,
  input  in_2,
  input  in_3,
  input  in_4,
  input  in_5,
  output [3:0] out_6,
  output out_7,
  output [4:0] S
);


  assign out_6 = {in_2, in_3, in_4, in_5};
  assign out_7 = in_1;
  assign S = {in_1, in_2, in_3, in_4, in_5};
endmodule

module Seletor (
  input  in_1,
  input  in_2,
  input  [4:0] in_3,
  input  [4:0] in_4,
  output out_5,
  output [3:0] out_6,
  output out_7,
  output [3:0] out_8
);

  wire [4:0] demultiplexer_1_out0, demultiplexer_1_out1, multiplexer_1_out;

  converte5para4 converte5para4_1 (.in_1(out_6), .out_3(out_5), .in_2(demultiplexer_1_out0));
  Demultiplexer #(.width(5), .enable("false")) demultiplexer_1 (
    .out0(demultiplexer_1_out0), .out1(demultiplexer_1_out1), .in(multiplexer_1_out), .sel(in_1));
  Multiplexer #(.width(5), .enable("false")) multiplexer_1 (
    .in0(in_3), .in1(in_4), .out(multiplexer_1_out), .sel(in_2));
  converte5para4 converte5para4_2 (.in_1(out_8), .out_3(out_7), .in_2(demultiplexer_1_out1));
endmodule

module MemoriaNumeroUser (
  input  Clock,
  input  [3:0] Entrada,
  output [3:0] \Saída 
);

  D_Flip_Flop d_ff_1 (.clk(Clock), .D(Entrada[0]), .Q(\Saída [0]));  // open: Qn, preset, en, reset
  D_Flip_Flop d_ff_2 (.clk(Clock), .D(Entrada[1]), .Q(\Saída [1]));  // open: Qn, preset, en, reset
  D_Flip_Flop d_ff_3 (.clk(Clock), .D(Entrada[2]), .Q(\Saída [2]));  // open: Qn, preset, en, reset
  D_Flip_Flop d_ff_4 (.clk(Clock), .D(Entrada[3]), .Q(\Saída [3]));  // open: Qn, preset, en, reset
endmodule

module RandomNumber (
  input  Clock,
  input  Reset,
  output [4:0] out_3,
  output [4:0] out_4
);

  wire converte5para4_1_out_3, converte5para4_2_out_3;
  wire [3:0] undriven, undriven_2;

  LED led_1 (.in(converte5para4_2_out_3));
  Hex_Digit_Display hex_digit_display_1 (.value(undriven_2));  // open: dp
  LED led_2 (.in(converte5para4_1_out_3));
  converte5para4 converte5para4_1 (.in_1(undriven_2), .out_3(converte5para4_1_out_3), .in_2(out_3));
  Random #(.width(5)) random_1 (.clk(Clock), .out(out_3), .clr(Reset));  // open: next
  Random #(.width(5)) random_2 (.clk(Clock), .out(out_4), .clr(Reset));  // open: next
  converte5para4 converte5para4_2 (.in_1(undriven), .out_3(converte5para4_2_out_3), .in_2(out_4));
  Hex_Digit_Display hex_digit_display_2 (.value(undriven));  // open: dp
endmodule

module converte5para4 (
  input  [3:0] in_1,
  input  [4:0] in_2,
  output out_3
);


  assign in_2[3:0] = in_1;
  assign out_3 = in_2[4];
endmodule

module Comparador (
  input  [4:0] X_random,
  input  [4:0] Y_random,
  input  [4:0] X_user,
  input  [4:0] Y_user
);
endmodule

module Somador (
  input  [4:0] in_1,
  input  [4:0] X,
  input  [4:0] Y
);

  wire Converte5_para_4_1_2_out_3, Converte5_para_4_1_out_3, xnor_1_out, xor_1_out;
  wire [3:0] undriven, undriven_2;
  wire [4:0] adder_1_out, demultiplexer_1_out0, demultiplexer_1_out1, multiplexer_1_out, not_1_out,
       subtractor_1_out;

  converte5para4 Converte5_para_4_1 (.in_1(undriven), .out_3(Converte5_para_4_1_out_3), .in_2(X));
  converte5para4 Converte5_para_4_1_2 (.in_1(undriven_2), .out_3(Converte5_para_4_1_2_out_3), .in_2(Y));
  Adder #(.width(4)) adder_1 (.a(undriven), .b(undriven_2), .out(adder_1_out[3:0]));  // open: cin, cout
  Subtractor #(.width(4)) subtractor_1 (.a(undriven), .b(undriven_2), .out(subtractor_1_out[3:0]));  // open: bin, bout
  Demultiplexer #(.width(5), .enable("false")) demultiplexer_1 (
    .out0(demultiplexer_1_out0), .out1(demultiplexer_1_out1), .in(multiplexer_1_out), .sel(xor_1_out));
  Multiplexer #(.width(5), .enable("false")) multiplexer_1 (
    .in0(adder_1_out), .in1(subtractor_1_out), .out(multiplexer_1_out), .sel(xnor_1_out));
  xnor xnor_1 (xnor_1_out, Converte5_para_4_1_out_3, Converte5_para_4_1_2_out_3);
  assign not_1_out = ~demultiplexer_1_out0;  // NOT_Gate not_1, 5 bits wide
  xor xor_1 (xor_1_out, Converte5_para_4_1_out_3, Converte5_para_4_1_2_out_3);
  Multiplexer #(.width(5), .enable("false")) multiplexer_2 (
    .in0(not_1_out), .in1(demultiplexer_1_out1), .out(in_1), .sel(xor_1_out));
  // Pins of 4 and 5 bits meet at subtractor_1_out
  // Pins of 4 and 5 bits meet at adder_1_out
endmodule
